# Fritzing sketch placa (saved by Fritzing 0.9.2b)
breadboards: 2

parts:
  LED1 = LED - 5mm [color="Red (633nm)" package="5 mm [THT]"]
  R1 = Resistor [tolerance=±5% resistance=300 package="2010 [SMD]"]
  LED2 = LED - 5mm [color="White (4500K)" package="5 mm [THT]"]
  R2 = Resistor [tolerance=±5% resistance=300 package="2010 [SMD]"]
  Componente1 = Bluetooth Mate Silver
  Componente2 = Arduino Mega 2560 (Rev3)
  D1 = LTE-302 [package=lte-302]
  PIR2 = PIR sensor

nets:
  N1: LED1.cathode, R1.Pin_0
  N2: R1.Pin_1, Componente2.D12_PWM
  N3: LED2.cathode, R2.Pin_0
  GND: LED2.anode, Componente1.TX_5V, Componente2.GND, D1.A, PIR2.GND
  N4: R2.Pin_1, Componente2.D4_PWM
  N5: Componente1.RTS_5V, Componente1.GND
  5V: Componente1.RX_5V, Componente2.5V, PIR2.VDD
  N6: Componente1.VCC, Componente2.D19/RX1
  N7: Componente1.CTS_5V, Componente2.D18/TX1
  N8: Componente2.D11_PWM, PIR2.SIG
  N9: Componente2.D9_PWM, D1.C
